// Logisim project HW2_2.circ as structural Verilog: 1 circuit, main circuit main
module main (
);

  wire adder_1_cout, adder_2_cout, adder_3_cout, adder_4_cout, and_1_out, and_2_out, nor_1_out, not_1_out,
       xor_1_out;
  wire [1:0] ALUControl;
  wire [3:0] adder_4_out, and_3_out, dipswitch_2_p4, multiplexer_1_out, or_1_out, undriven, xor_2_out;

  xor xor_1 (xor_1_out, adder_2_cout, adder_1_cout);
  and and_1 (and_1_out, xor_1_out, not_1_out);
  LED led_1 (.in(and_1_out));
  LED led_2 (.in(multiplexer_1_out[3]));
  not not_1 (not_1_out, ALUControl[1]);
  and and_2 (and_2_out, not_1_out, adder_1_cout);
  LED led_3 (.in(and_2_out));
  nor nor_1 (nor_1_out, multiplexer_1_out[3], multiplexer_1_out[2], multiplexer_1_out[1], multiplexer_1_out[0]);
  LED led_4 (.in(nor_1_out));
  assign and_3_out = dipswitch_2_p4 & undriven;  // AND_Gate and_3, 4 bits wide
  // DipSwitch #(.number(4)) dipswitch_1: pin names not known
  assign or_1_out = dipswitch_2_p4 | undriven;  // OR_Gate or_1, 4 bits wide
  Multiplexer #(.select(2), .width(4)) multiplexer_1 (
    .in0(adder_4_out), .in1(adder_4_out), .in2(and_3_out), .in3(or_1_out), .out(multiplexer_1_out),
    .sel(ALUControl));
  LED led_5 (.in(multiplexer_1_out[3]));
  LED led_6 (.in(multiplexer_1_out[2]));
  LED led_7 (.in(multiplexer_1_out[1]));
  Adder #(.width(1)) adder_1 (
    .a(xor_2_out[3]), .b(dipswitch_2_p4[3]), .out(adder_4_out[3]), .cin(adder_2_cout), .cout(adder_1_cout));
  LED led_8 (.in(multiplexer_1_out[0]));
  // DipSwitch #(.number(4)) dipswitch_2: pin names not known; wires that end beside it: dipswitch_2_p4[3], dipswitch_2_p4[2], dipswitch_2_p4[1], dipswitch_2_p4[0]
  assign xor_2_out = undriven ^ {4{ALUControl[0]}};  // XOR_Gate xor_2, 4 bits wide
  Adder #(.width(1)) adder_2 (
    .a(xor_2_out[2]), .b(dipswitch_2_p4[2]), .out(adder_4_out[2]), .cin(adder_3_cout), .cout(adder_2_cout));
  Adder #(.width(1)) adder_3 (
    .a(xor_2_out[1]), .b(dipswitch_2_p4[1]), .out(adder_4_out[1]), .cin(adder_4_cout), .cout(adder_3_cout));
  // DipSwitch #(.number(2)) dipswitch_3: pin names not known
  Adder #(.width(1)) adder_4 (
    .a(xor_2_out[0]), .b(dipswitch_2_p4[0]), .out(adder_4_out[0]), .cin(ALUControl[0]), .cout(adder_4_cout));

  // Notes on the sheet:
  //   oVerfllow
  //   Negative
  //   Carry
  //   Zero
  //   A
  //   Result
  //   B
endmodule
