// Logisim project HW2_3.circ as structural Verilog: 1 circuit, main circuit main
module main (
);

  wire dipswitch_1_sw2, dipswitch_1_sw3, not_1_out, not_2_out, or_1_out;

  DipSwitch #(.number(4)) dipswitch_1 (.sw2(dipswitch_1_sw2), .sw3(dipswitch_1_sw3));  // open: sw1, sw4
  not not_1 (not_1_out, dipswitch_1_sw2);
  or or_1 (or_1_out, dipswitch_1_sw3, not_1_out);
  not not_2 (not_2_out, or_1_out);
  LED led_1 (.in(not_1_out));
  LED led_2 (.in(or_1_out));
  LED led_3 (.in(not_2_out));
  LED led_4 (.in(dipswitch_1_sw2));

  // Notes on the sheet:
  //   V C Z N
  //   LO
  //   LS
  //   HI
  //   HS
endmodule
