// Logisim project HW2_4a.circ as structural Verilog: 1 circuit, main circuit main
module main (
);

  wire and_1_out, and_2_out, and_3_out, and_4_out, clock_1_out, d_ff_1_q, d_ff_1_qn, d_ff_2_q, d_ff_2_qn,
       dipswitch_1_sw1, dipswitch_1_sw2, nor_1_out, nor_2_out, not_1_out, not_2_out, not_3_out, or_1_out,
       xor_1_out;

  not not_1 (not_1_out, dipswitch_1_sw1);
  not not_2 (not_2_out, dipswitch_1_sw2);
  DipSwitch #(.number(2)) dipswitch_1 (.sw1(dipswitch_1_sw1), .sw2(dipswitch_1_sw2));
  and and_1 (and_1_out, d_ff_1_qn, d_ff_2_qn, not_1_out);
  and and_2 (and_2_out, d_ff_1_q, d_ff_2_qn, not_2_out);
  xor xor_1 (xor_1_out, d_ff_1_q, d_ff_2_q);
  or or_1 (or_1_out, and_1_out, and_2_out);
  D_Flip_Flop d_ff_1 (.D(xor_1_out), .clk(clock_1_out), .Q(d_ff_1_q), .Qn(d_ff_1_qn));  // open: preset, reset
  D_Flip_Flop d_ff_2 (.D(or_1_out), .clk(clock_1_out), .Q(d_ff_2_q), .Qn(d_ff_2_qn));  // open: preset, reset
  Clock clock_1 (.out(clock_1_out));
  not not_3 (not_3_out, d_ff_1_q);
  and and_3 (and_3_out, not_3_out, d_ff_2_q);
  and and_4 (and_4_out, d_ff_1_q, d_ff_2_q);
  nor nor_1 (nor_1_out, not_3_out, and_4_out);
  nor nor_2 (nor_2_out, d_ff_1_q, and_3_out);
  LED led_1 (.in(d_ff_1_q));
  LED led_2 (.in(and_3_out));
  LED led_3 (.in(nor_2_out));
  LED led_4 (.in(not_3_out));
  LED led_5 (.in(and_4_out));
  LED led_6 (.in(nor_1_out));
  LED led_7 (.in(not_3_out));
  LED led_8 (.in(and_4_out));
  LED led_9 (.in(nor_1_out));
  LED led_10 (.in(d_ff_1_q));
  LED led_11 (.in(and_3_out));
  LED led_12 (.in(nor_2_out));

  // Notes on the sheet:
  //   TA TB
  //   s1
  //   s0
  //   Academic
  //   TALA
  //   Bravado
  //   TBLB
  //   TBLB
  //   Blvd.
  //   TALA
  //   Ave.
endmodule
