// Logisim project HW2_4b.circ as structural Verilog: 1 circuit, main circuit main
module main (
);

  wire and_1_out, and_2_out, and_3_out, and_4_out, and_5_out, and_6_out, and_7_out, and_8_out, and_9_out,
       and_10_out, and_11_out, and_12_out, and_13_out, and_14_out, clock_1_out, d_ff_1_q, d_ff_1_qn,
       d_ff_2_q, d_ff_2_qn, d_ff_3_q, d_ff_3_qn, dipswitch_1_p1, dipswitch_1_p2, nor_1_out, nor_2_out,
       nor_3_out, not_1_out, not_2_out, or_1_out, or_2_out, or_3_out, or_4_out, or_5_out;

  not not_1 (not_1_out, dipswitch_1_p2);
  not not_2 (not_2_out, dipswitch_1_p1);
  and and_1 (and_1_out, d_ff_1_q, d_ff_2_qn, d_ff_3_qn);
  and and_2 (and_2_out, d_ff_1_qn, d_ff_2_q, d_ff_3_q, not_2_out);
  and and_3 (and_3_out, d_ff_1_qn, d_ff_2_qn, d_ff_3_q);
  and and_4 (and_4_out, d_ff_1_qn, d_ff_2_q, d_ff_3_q, dipswitch_1_p1);
  and and_5 (and_5_out, d_ff_1_qn, d_ff_2_q, d_ff_3_qn);
  and and_6 (and_6_out, d_ff_1_q, d_ff_2_qn, d_ff_3_qn);
  and and_7 (and_7_out, d_ff_1_qn, d_ff_2_q, d_ff_3_qn);
  and and_8 (and_8_out, d_ff_1_qn, d_ff_2_q, d_ff_3_q, dipswitch_1_p1);
  and and_9 (and_9_out, not_1_out, d_ff_1_qn, d_ff_2_qn, d_ff_3_qn);
  // DipSwitch #(.number(2)) dipswitch_1: pin names not known; wires that end beside it: dipswitch_1_p1, dipswitch_1_p2
  or or_1 (or_1_out, and_1_out, and_2_out);
  or or_2 (or_2_out, and_3_out, and_4_out, and_5_out);
  or or_3 (or_3_out, and_6_out, and_7_out, and_8_out, and_9_out);
  D_Flip_Flop d_ff_1 (.D(or_1_out), .clk(clock_1_out), .Q(d_ff_1_q), .Qn(d_ff_1_qn));  // open: preset, reset
  D_Flip_Flop d_ff_2 (.D(or_2_out), .clk(clock_1_out), .Q(d_ff_2_q), .Qn(d_ff_2_qn));  // open: preset, reset
  D_Flip_Flop d_ff_3 (.D(or_3_out), .clk(clock_1_out), .Q(d_ff_3_q), .Qn(d_ff_3_qn));  // open: preset, reset
  Clock clock_1 (.out(clock_1_out));
  and and_10 (and_10_out, d_ff_1_q, ~d_ff_2_q, ~d_ff_3_q);  // AND_Gate
  and and_11 (and_11_out, ~d_ff_2_q, d_ff_3_q);  // AND_Gate
  nor nor_1 (nor_1_out, d_ff_3_q, d_ff_1_q);
  and and_12 (and_12_out, ~d_ff_1_q, ~d_ff_2_q, d_ff_3_q);  // AND_Gate
  and and_13 (and_13_out, ~d_ff_1_q, d_ff_2_q);  // AND_Gate
  and and_14 (and_14_out, d_ff_1_q, ~d_ff_2_q);  // AND_Gate
  or or_4 (or_4_out, and_11_out, nor_1_out);
  or or_5 (or_5_out, and_13_out, and_14_out);
  nor nor_2 (nor_2_out, and_10_out, or_4_out);
  nor nor_3 (nor_3_out, and_12_out, or_5_out);
  LED led_1 (.in(or_5_out));
  LED led_2 (.in(and_12_out));
  LED led_3 (.in(nor_3_out));
  LED led_4 (.in(or_4_out));
  LED led_5 (.in(and_10_out));
  LED led_6 (.in(nor_2_out));
  LED led_7 (.in(or_4_out));
  LED led_8 (.in(and_10_out));
  LED led_9 (.in(nor_2_out));
  LED led_10 (.in(or_5_out));
  LED led_11 (.in(and_12_out));
  LED led_12 (.in(nor_3_out));

  // Notes on the sheet:
  //   TB
  //   not s2
  //   ~TB
  //   ~TA
  //   not s0
  //   s2
  //   s1
  //   not s1
  //   so
  //   TB
  //   TA
  //   s2
  //   s1
  //   s0
  //   LB0
  //   LB1
  //   LA0
  //   LA1
  //   Academic
  //   TALA
  //   Bravado
  //   TBLB
  //   TBLB
  //   Blvd.
  //   TALA
  //   Ave.
endmodule
