// Logisim project HW2_5b.circ as structural Verilog: 1 circuit, main circuit main
module main (
);

  wire button_1_out, clock_1_out, d_ff_1_q, d_ff_2_q, d_ff_3_q, d_ff_4_q, d_ff_4_qn;

  Clock clock_1 (.out(clock_1_out));
  Button button_1 (.out(button_1_out));
  D_Flip_Flop #(.trigger("high")) d_ff_1 (
    .D(d_ff_4_qn), .clk(clock_1_out), .Q(d_ff_1_q), .reset(button_1_out));  // open: Qn, preset
  D_Flip_Flop #(.trigger("high")) d_ff_2 (
    .D(d_ff_1_q), .clk(clock_1_out), .Q(d_ff_2_q), .reset(button_1_out));  // open: Qn, preset
  LED led_1 (.in(d_ff_1_q));
  LED led_2 (.in(d_ff_2_q));
  LED led_3 (.in(d_ff_3_q));
  LED led_4 (.in(d_ff_4_q));
  D_Flip_Flop #(.trigger("high")) d_ff_3 (
    .D(d_ff_2_q), .clk(clock_1_out), .Q(d_ff_3_q), .reset(button_1_out));  // open: Qn, preset
  D_Flip_Flop #(.trigger("high")) d_ff_4 (
    .D(d_ff_3_q), .clk(clock_1_out), .Q(d_ff_4_q), .Qn(d_ff_4_qn), .reset(button_1_out));  // open: preset
endmodule
