// Logisim project HW2_6.circ as structural Verilog: 1 circuit, main circuit main
module main (
);

  wire B, Clk, decoder_1_out0, decoder_1_out1, decoder_1_out2, decoder_1_out3, nor_1_out, not_2_out, RegW,
       Reset, ZFlag;
  wire [1:0] Op;
  wire [5:0] adder_1_out, BTA, multiplexer_1_out, register_1_q;
  wire [7:0] adder_2_out, and_1_out, multiplexer_2_out, multiplexer_3_out, multiplexer_4_out, not_1_out,
       register_2_q, register_3_q, register_4_q, register_5_q;

  Button button_1 (.out(Reset));
  Decoder #(.select(2)) decoder_1 (
    .out0(decoder_1_out0), .out1(decoder_1_out1), .out2(decoder_1_out2), .out3(decoder_1_out3),
    .sel(BTA[1:0]), .en(RegW));
  Register #(.width(6)) register_1 (.D(multiplexer_1_out), .clk(Clk), .Q(register_1_q), .clr(Reset));  // open: en
  Multiplexer #(.width(6)) multiplexer_1 (.in0(adder_1_out), .in1(BTA), .out(multiplexer_1_out), .sel(B));
  Register register_2 (.D(multiplexer_4_out), .en(decoder_1_out0), .clk(Clk), .Q(register_2_q), .clr(Reset));
  Register register_3 (.D(multiplexer_4_out), .en(decoder_1_out1), .clk(Clk), .Q(register_3_q), .clr(Reset));
  Register register_4 (.D(multiplexer_4_out), .en(decoder_1_out2), .clk(Clk), .Q(register_4_q), .clr(Reset));
  Register register_5 (.D(multiplexer_4_out), .en(decoder_1_out3), .clk(Clk), .Q(register_5_q), .clr(Reset));
  Adder #(.width(6)) adder_1 (.a(register_1_q), .b(6'b000001), .out(adder_1_out));  // open: cin, cout
  ROM #(.addrWidth(6)) rom_1 (.addr(register_1_q), .data({Op, BTA}));
  Hex_Digit_Display hex_digit_display_1 (.value(register_5_q[7:4]));  // open: dp
  Multiplexer #(.select(2), .width(8)) multiplexer_2 (
    .in0(register_2_q), .in1(register_3_q), .in2(register_4_q), .in3(register_5_q), .out(multiplexer_2_out),
    .sel(BTA[5:4]));
  Multiplexer #(.select(2), .width(8)) multiplexer_3 (
    .in0(register_2_q), .in1(register_3_q), .in2(register_4_q), .in3(register_5_q), .out(multiplexer_3_out),
    .sel(BTA[3:2]));
  Hex_Digit_Display hex_digit_display_2 (.value(register_5_q[3:0]));  // open: dp
  nand nand_1 (RegW, Op[1], Op[0]);
  Register #(.width(1)) register_6 (.D(nor_1_out), .en(RegW), .clk(Clk), .Q(ZFlag), .clr(Reset));
  Adder adder_2 (.a(multiplexer_2_out), .b(multiplexer_3_out), .out(adder_2_out));  // open: cin, cout
  assign and_1_out = multiplexer_2_out & multiplexer_3_out;  // AND_Gate and_1, 8 bits wide
  assign not_1_out = ~multiplexer_2_out;  // NOT_Gate not_1, 8 bits wide
  nor nor_1 (nor_1_out, multiplexer_4_out[0], multiplexer_4_out[1], multiplexer_4_out[2], multiplexer_4_out[3], multiplexer_4_out[4], multiplexer_4_out[5], multiplexer_4_out[6], multiplexer_4_out[7]);
  not not_2 (not_2_out, ZFlag);
  and and_2 (B, Op[0], Op[1], not_2_out);
  Multiplexer #(.select(2), .width(8)) multiplexer_4 (
    .in0(adder_2_out), .in1(and_1_out), .in2(not_1_out), .out(multiplexer_4_out), .sel(Op));  // open: in3
  Clock clock_1 (.out(Clk));

  // Other names for the same wires on the sheet: Rd[1:0] = BTA[1:0]; Rm[1:0] = BTA[3:2]; Rn[1:0] = BTA[5:4]

  // Notes on the sheet:
  //   PC+1
  //   contents of rom_1 (hex, n*v repeats v):
  //   90 44 81 15 91 43 16 2a 2a 4*1a a2 26 d4 7d 10 5 43 57 81 45 91 15 91 26 26 d0 7f de
endmodule
